# Fritzing sketch NEUROX draft 1 (saved by Fritzing 0.9.3b)
breadboards: 2

parts:
  IMU_Sensor_(ARM) = Tri-Axis Gyro Breakout - L3G4200D
  WARM_Water_Pump = DC Motor
  U3 = SWITCH_SPDT [package=kps-1290]
  MH-ET_LIVE_ESP32_DEVKIT1 = MH-ET LIVE ESP32 DEVKIT 38 pins
  Hot_Temp_Sensor = DS18B20 1-Wire Temperature Sensor [part_number=DS18B20]
  Cold_Temp_Sensor = DS18B20 1-Wire Temperature Sensor [part_number=DS18B20]
  IMU_Sensor_(Forearm) = Tri-Axis Gyro Breakout - L3G4200D
  U7 = RELAY [package=relay-jzc]
  U8 = RELAY [package=relay-jzc]
  COLD_Water_Pump = DC Motor
  Air_Pump_(pneumatic_pockets) = Lilypad Vibe Motor
  Heating_pad = LED - 5mm [color="Red (633nm)" package="5 mm [THT]"]
  U9 = RELAY [package=relay-jzc]
  U10 = RELAY [package=relay-jzc]
  12V_battery_pack = LIPO-2000mAh [package=lipo-2000]
  U11 = SWITCH_SPDT [package=kps-1290]
  5V_supply_(battery_pack) = 4 x AAA Battery Mount
  R1 = Resistor [tolerance=±5% resistance=4.7k package="1206 [SMD]"]
  R2 = Resistor [tolerance=±5% resistance=4.7k package="1206 [SMD]"]
  MH-ET_LIVE_ESP32_DEVKIT2 = MH-ET LIVE ESP32 DEVKIT 38 pins
  Vibration_Motor_(Forearm) = Vibration Motor- ROB-08449 [package=vibe-motor-10mm]
  Q1 = Basic FET N-Channel [package="D2Pak [SMD]"]
  Q2 = Basic FET N-Channel [package="D2Pak [SMD]"]
  Vibration_Motor_(Arm) = Vibration Motor- ROB-08449 [package=vibe-motor-10mm]
  part = Battery
  U12 = SWITCH_SPDT [package=kps-1290]
  U14 = RELAY [package=relay-jzc]
  Solenoid_valve_(Release_Air) = Lilypad Vibe Motor

nets:
  VCC: IMU_Sensor_(ARM).VCC, IMU_Sensor_(ARM).SDO, IMU_Sensor_(Forearm).VCC, MH-ET_LIVE_ESP32_DEVKIT2.3V3, U12.P
  N1: IMU_Sensor_(ARM).SCL, IMU_Sensor_(Forearm).SCL, MH-ET_LIVE_ESP32_DEVKIT2.IO5
  N2: IMU_Sensor_(ARM).SDA, IMU_Sensor_(Forearm).SDA, MH-ET_LIVE_ESP32_DEVKIT2.IO4
  N3: WARM_Water_Pump.pin_1, U7.NO
  GND: WARM_Water_Pump.pin_2, U3.O, COLD_Water_Pump.pin_2, Air_Pump_(pneumatic_pockets).GND, Heating_pad.cathode, U9.COIL2, U10.COIL2, 12V_battery_pack.-, U14.COIL2, Solenoid_valve_(Release_Air).GND
  N4: U3.P, U7.MAIN, U8.MAIN, U9.MAIN, U10.MAIN, U14.MAIN
  N5: U3.S, 12V_battery_pack.+
  VDD: MH-ET_LIVE_ESP32_DEVKIT1.3V3, Hot_Temp_Sensor.VDD, Cold_Temp_Sensor.VDD, U7.COIL1, U8.COIL1, U9.COIL1, U10.COIL1, R1.Pin_0, R2.Pin_0, U14.COIL1
  N6: MH-ET_LIVE_ESP32_DEVKIT1.CMD, MH-ET_LIVE_ESP32_DEVKIT1.5V, U11.P
  GND_2: MH-ET_LIVE_ESP32_DEVKIT1.GND, MH-ET_LIVE_ESP32_DEVKIT1.IO19, Hot_Temp_Sensor.GND, Cold_Temp_Sensor.GND, U7.COIL2, U7.NC, U8.COIL2, U11.S, 5V_supply_(battery_pack).-
  N7: MH-ET_LIVE_ESP32_DEVKIT1.IO22, U9.NC
  N8: MH-ET_LIVE_ESP32_DEVKIT1.IO21, U8.NC
  N9: MH-ET_LIVE_ESP32_DEVKIT1.IO18, U14.NC
  N10: MH-ET_LIVE_ESP32_DEVKIT1.IO17, Hot_Temp_Sensor.DQ, R2.Pin_1
  N11: MH-ET_LIVE_ESP32_DEVKIT1.IO16, Cold_Temp_Sensor.DQ, R1.Pin_1
  N12: MH-ET_LIVE_ESP32_DEVKIT1.IO4, U10.NC
  GND_3: IMU_Sensor_(Forearm).GND, MH-ET_LIVE_ESP32_DEVKIT2.GND, Vibration_Motor_(Forearm).+, Q1.source, Q2.source, Vibration_Motor_(Arm).+, part.-, U12.O
  N13: U8.NO, COLD_Water_Pump.pin_1
  N14: Air_Pump_(pneumatic_pockets).Supply, U10.NO
  N15: Heating_pad.anode, U9.NO
  N16: U11.O, 5V_supply_(battery_pack).+
  N17: MH-ET_LIVE_ESP32_DEVKIT2.IO17, Q2.Gate
  N18: MH-ET_LIVE_ESP32_DEVKIT2.IO16, Q1.Gate
  N19: Vibration_Motor_(Forearm).-, Q2.drain
  N20: Q1.drain, Vibration_Motor_(Arm).-
  N21: part.+, U12.S
  N22: U14.NO, Solenoid_valve_(Release_Air).Supply

custom parts:
  MH-ET LIVE ESP32 DEVKIT 38 pins: http://mh.nodebb.com/topic/2/mh-et-live-esp32-devkit
